# Fritzing sketch fritzing_sketch_2.0 (saved by Fritzing 0.9.3b)
breadboards: 1

parts:
  Part1 = Adafruit Feather 32u4 FONA [part_number="Adafruit #3027"]
  LCD1 = LCD screen [part_number="1602A Char LCD / 3.3V / Standard ST7066/HD44780"]
  DS1 = DS18B20 1-Wire Temperature Sensor [part_number=DS18B20]
  R1 = Resistor [tolerance=±5% resistance=220 package="2512 [SMD]"]
  R2 = Resistor [tolerance=±5% resistance=100 package="2512 [SMD]"]
  J1 = Piezo Speaker
  BATT1 = LiPoly Battery (1300mAh)  # not connected
  R3 = Trimmer Potentiometer [maximum_resistance=10kΩ package=THT]
  ANT1 = Antenna  # not connected
  R4 = Resistor [tolerance=±5% resistance=1M package="0603 [SMD]"]
  R5 = Resistor [tolerance=±5% resistance=1M package="0603 [SMD]"]

nets:
  N1: Part1.KEY, LCD1.DB4
  N2: Part1.1, LCD1.DB5
  N3: Part1.A0, R4.Pin_0, R5.Pin_1
  GND: Part1.GND, LCD1.VSS, LCD1.R/W, LCD1.LED-, DS1.GND, J1.pin1, R3.leg1, R5.Pin_0
  VDD: Part1.+3V3, LCD1.VDD, DS1.VDD, R1.Pin_0, R3.leg2
  N4: Part1.VBUS, R4.Pin_1
  N5: Part1.12, LCD1.RS
  N6: Part1.11, LCD1.E
  N7: Part1.10, R2.Pin_0
  N8: Part1.5_UART_DTR, DS1.DQ
  N9: Part1.3, LCD1.DB6
  N10: Part1.2, LCD1.DB7
  N11: LCD1.V0, R3.wiper
  N12: LCD1.LED+, R1.Pin_1
  N13: R2.Pin_1, J1.pin2

custom parts:
  Adafruit Feather 32u4 FONA: This is the Adafruit Feather 32u4 FONA - our take on an 'all-in-one' Arduino-compatible + audio/sms/data capable cellular with built in USB and battery charging. Its an Adafruit Feather 32u4 with a FONA800 module, ready to rock! We have other boards and accessories in the Feather family, check'em out here. At the Feather 32u4's heart is at ATmega32u4 clocked at 8 MHz and at 3.3V logic, a chip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
  LiPoly Battery (1300mAh): Lithium Ion Polymer Battery (1300mAh)
